# Fritzing sketch three_joysticks (saved by Fritzing 1.0.5)
breadboards: 1

parts:
  U1 = Thumb Joystick [package=joystick]
  R1 = TRIMPOT [maximum_resistance=10kΩ knob_status=50% power=0.5W package=3386u]
  R2 = TRIMPOT [maximum_resistance=10kΩ knob_status=50% power=0.5W package=3386u]
  Part1 = Arduino Uno (Rev3) - ICSP
  S2 = JOYSTICK_MINI [package=joystick_mini]

nets:
  N1: U1.SEL+, Part1.D2
  N2: U1.V+, U1.H+, R1.CW, R2.CW, Part1.5V
  N3: U1.SEL-, U1.H-, U1.V-, R1.CCW, R2.CCW, Part1.GND, S2.Common
  N4: U1.V, Part1.A1
  N5: U1.H, Part1.A0
  N6: R1.WIPER, Part1.A2
  N7: R2.WIPER, Part1.A3
  N8: Part1.D3_PWM, S2.S3
  N9: Part1.D4, S2.S6
  N10: Part1.D5_PWM, S2.S1
  N11: Part1.D6_PWM, S2.S4
  N12: Part1.D7, S2.Center

notes:
  Thumb Joystick
  Thumb Slide Joystick
  Horizontal Ax.
  Vertical Ax.
  5-way Tactile Switch
  5-Way Tactile Switch. This Fritzing part pinout does not correspond to the original.
  SparkFun SKU: COM-10063
  SparkFun SKU: COM-09426
  SparkFun SKU: COM-09032
  UCI v2.0, This sketch defines the wiring of 3 joysticks connected to Arduino UNO board., O.A.M.F.
  Vertical Axis
  Horizontal Axis

custom parts:
  JOYSTICK_MINI: Small 5-way tactile joystick, COM-10063 4UCON SF303GJ26
